# Fritzing sketch rc522(bckup) (saved by Fritzing 0.9.0b)
circuit board: 8.46667cm x 5.64444cm
breadboards: 1

parts:
  LED1 = RGB LED - (4 legs) [package="5 mm [THT]"]
  R3 = Resistor [tolerance=±5% resistance=220 package=THT]
  SG1 = Buzzer 12mm [package=buzzer-12mm-ns]
  S1 = SWITCH-MOMENTARY-2 [package=tactile-pth-12mm]
  R4 = Resistor [tolerance=±5% resistance=220 package="0805 [SMD]"]
  Часть3 = Arduino Nano (Rev3.0)
  R5 = Resistor [tolerance=±5% resistance=220 package=THT]
  R6 = Resistor [tolerance=±5% resistance=220 package=THT]
  U4 = G3VM-61E1 [package=g3vm-61e1]
  VCC1 = Battery block 9V
  R7 = Resistor [tolerance=±5% resistance=4.7k package=THT]
  R8 = Resistor [tolerance=±5% resistance=4.7k package=THT]

nets:
  N1: LED1.red_cathode, R3.Pin_0
  N2: LED1.common_anode, SG1.2, R4.Pin_0, Часть3.GND, U4.P$4
  N3: LED1.green_cathode, R5.Pin_0
  N4: LED1.blue_cathode, R6.Pin_0
  N5: R3.Pin_1, Часть3.D5
  N6: SG1.1, Часть3.D8
  N7: S1.2, Часть3.5V, U4.P$5, R7.Pin_1, R8.Pin_1
  N8: Часть3.D3, U4.P$6
  N9: Часть3.D6, R5.Pin_1
  N10: Часть3.D7, R6.Pin_1
  N11: Часть3.D10, R8.Pin_0
  N12: Часть3.D11/MOSI, R7.Pin_0
  N13: U4.P$1, VCC1.+
